// Logisim project ISA.circ as structural Verilog: 3 circuits, main circuit Main
module Main (
);

  wire b_reg_1_p2, clock_1_out;
  wire [7:0] UC_data;
  wire [31:0] b_reg_1_p3, multiplexer_1_out, ula_1_p3;

  Clock clock_1 (.out(clock_1_out));
  Register PC (.clk(clock_1_out));  // open: D, en, Q, clr
  ROM #(.addrWidth(24), .dataWidth(24)) rom_1 ();  // open: addr, data
  // B_REG b_reg_1: pin names not known; wires that end beside it: clock_1_out, b_reg_1_p2, b_reg_1_p3
  Multiplexer #(.width(32)) multiplexer_1 (.in0(b_reg_1_p3), .out(multiplexer_1_out));  // open: in1, sel
  // ULA ula_1: pin names not known; wires that end beside it: b_reg_1_p2, multiplexer_1_out, ula_1_p3
  ROM UC (.data(UC_data));  // open: addr
  RAM #(.addrWidth(24), .dataWidth(32)) M_DADOS (
    .addr(ula_1_p3[23:0]), .we(UC_data[0]), .oe(1'b1), .clk(clock_1_out), .din(b_reg_1_p3));  // open: dout
  // Pins of 1 and 8 bits meet at UC_data

  // Notes on the sheet:
  //   contents of rom_1 (hex, n*v repeats v):
  //   443 8443 10443 18443 20443 28443 30443 38443 808800 908800 a08800 b08800 c08800 d08800 e08800 f08800
  //   10e0 2010e0 4010e0 6010e0 8010e0 840000 608800
endmodule

module ULA (
  input  [11:0] rs1,
  input  [11:0] rs2,
  input  [3:0] ULA_CONTROL,
  output ZERO,
  output [11:0] SAIDA
);

  wire comparator_1_lt;
  wire [11:0] adder_1_out, and_1_out, bit_extender_1_out, multiplexer_1_out, not_1_out, or_1_out,
       shifter_1_out, shifter_2_out, subtractor_1_out, xor_1_out;

  Adder #(.width(12)) adder_1 (.a(rs1), .b(rs2), .out(adder_1_out));  // open: cin, cout
  Subtractor #(.width(12)) subtractor_1 (.a(rs1), .b(rs2), .out(subtractor_1_out));  // open: bin, bout
  Shifter #(.width(12)) shifter_1 (.in(rs1), .\dist (4'b0001), .out(shifter_1_out));
  Shifter #(.shift("lr"), .width(12)) shifter_2 (.in(rs1), .\dist (4'b0001), .out(shifter_2_out));
  assign and_1_out = rs1 & rs2;  // AND_Gate and_1, 12 bits wide
  assign or_1_out = rs1 | rs2;  // OR_Gate or_1, 12 bits wide
  assign xor_1_out = rs1 ^ rs2;  // XOR_Gate xor_1, 12 bits wide
  assign not_1_out = ~rs1;  // NOT_Gate not_1, 12 bits wide
  Comparator #(.width(12)) comparator_1 (.a(rs1), .b(rs2), .lt(comparator_1_lt));  // open: gt, eq
  assign bit_extender_1_out = {{11{comparator_1_lt}}, comparator_1_lt};  // Bit_Extender bit_extender_1
  Multiplexer #(.select(4), .width(12)) multiplexer_1 (
    .in0(adder_1_out), .in1(subtractor_1_out), .in2(shifter_1_out), .in3(shifter_2_out), .in4(and_1_out),
    .in5(or_1_out), .in6(xor_1_out), .in7(not_1_out), .in8(bit_extender_1_out), .out(multiplexer_1_out),
    .sel(ULA_CONTROL));  // open: in9, in10, in11, in12, in13, in14, in15
  nor nor_1 (ZERO, multiplexer_1_out[0], multiplexer_1_out[1], multiplexer_1_out[2], multiplexer_1_out[3], multiplexer_1_out[4], multiplexer_1_out[5], multiplexer_1_out[6], multiplexer_1_out[7], multiplexer_1_out[8], multiplexer_1_out[9], multiplexer_1_out[10], multiplexer_1_out[11]);
endmodule

module B_REG (
  input  [11:0] DATA,
  input  CLK,
  input  [1:0] RD,
  input  [1:0] RS1,
  input  [1:0] RS2,
  output [11:0] SAIDA_1,
  output [11:0] SAIDA_2
);

  wire decoder_1_out0, decoder_1_out1, decoder_1_out2, decoder_1_out3;
  wire [11:0] R0, R1, R2, R3;

  Decoder #(.select(2)) decoder_1 (
    .out0(decoder_1_out0), .out1(decoder_1_out1), .out2(decoder_1_out2), .out3(decoder_1_out3), .sel(RD));  // open: en
  Register #(.width(12)) register_1 (.D(DATA), .en(decoder_1_out0), .Q(R0));  // open: clk, clr
  Register #(.width(12)) register_2 (.D(DATA), .en(decoder_1_out1), .Q(R1));  // open: clk, clr
  Register #(.width(12)) register_3 (.D(DATA), .en(decoder_1_out2), .Q(R2));  // open: clk, clr
  Register #(.width(12)) register_4 (.D(DATA), .en(decoder_1_out3), .Q(R3));  // open: clk, clr
  Multiplexer #(.select(2), .width(12)) multiplexer_1 (
    .in0(R0), .in1(R1), .in2(R2), .in3(R3), .out(SAIDA_1), .sel(RS1));
  Multiplexer #(.select(2), .width(12)) multiplexer_2 (
    .in0(R0), .in1(R1), .in2(R2), .in3(R3), .out(SAIDA_2), .sel(RS2));
endmodule
